# Fritzing sketch atmotest (saved by Fritzing 0.6.4b)
breadboards: 1

parts:
  Arduino1 = Arduino
  IC1 = ULN2003A [package="DIP16 [THT]"]
  Power_plug1 = Power plug
  LED1 = LED - 5mm [color="Red (633nm)" package="5 mm [THT]"]
  LED2 = LED - 5mm [color="Green (555nm)" package="5 mm [THT]"]
  LED3 = LED - 5mm [color="Blue (430nm)" package="5 mm [THT]"]

nets:
  GND: Arduino1.GND, IC1.0V, Power_plug1.GND
  N1: Arduino1.D11, IC1.In_1
  N2: Arduino1.D10, IC1.In_2
  N3: Arduino1.D9, IC1.In_3
  N4: IC1.Out_3, LED3.cathode
  N5: IC1.Out_2, LED2.cathode
  N6: IC1.Out_1, LED1.cathode
  N7: Power_plug1.VCC, LED1.anode, LED2.anode, LED3.anode
